// Digital circuit CPU4bit.dig as structural Verilog
module CPU4bit (
  input  clk,
  input  [1:0] InstructionMemory_ctrl,
  input  [3:0] InstructionMemory_dataInput,
  input  [3:0] Dummy,
  output [1:0] IR_HI_1_0,
  output [1:0] IR_HI_3_2,
  output [1:0] IR_LO_1_0,
  output [1:0] IR_LO_3_2,
  output [4:0] state,
  output [3:0] Final_Output,
  output PC_inc,
  output [3:0] IP,
  output IR_HI_Write,
  output IR_LO_Write,
  output [3:0] ALU_out
);

  wire and_4_out, not_3_out, State_Transition_p5, xor_1_out;
  wire [1:0] multiplexer_1_out, multiplexer_2_out, multiplexer_3_out, multiplexer_6_out, not_1_out, not_2_out;
  wire [2:0] and_1_out;
  wire [3:0] demultiplexer_1_out_0, demultiplexer_1_out_1, Instruction_Memory_data_output, multiplexer_7_out,
       multiplexer_8_out, Register_File_readdata_1, Register_File_readdata_2;
  wire [7:0] multiplexer_4_out, multiplexer_5_out;

  Multiplexer #(.Bits(2)) multiplexer_1 (.sel(PC_inc), .in_0(2'b10), .in_1(2'b11), .out(multiplexer_1_out));
  Program_Counter Program_Counter (
    .Clock(clk), .Input(4'b0000), .Clear_Store_Load_Implement(multiplexer_1_out), .Inc(4'b0001), .Output(IP));
  // Five_State_Transition State_Transition: pin names not known; wires that end beside it: clk, state, IR_HI_Write, IR_LO_Write, State_Transition_p5, PC_inc
  Registers_DRAM Instruction_Memory (
    .Address_Bus(IP), .Clock(clk), .Control_Bus(InstructionMemory_ctrl),
    .Data_Bus(InstructionMemory_dataInput), .Data_Output(Instruction_Memory_data_output));
  Demultiplexer #(.Bits(4)) demultiplexer_1 (
    .sel(IP[0]), .in(Instruction_Memory_data_output), .out_0(demultiplexer_1_out_0),
    .out_1(demultiplexer_1_out_1));
  Multiplexer #(.Bits(2)) multiplexer_2 (.sel(IR_LO_Write), .in_0(2'b10), .in_1(2'b01), .out(multiplexer_2_out));
  Multiplexer #(.Bits(2)) multiplexer_3 (.sel(IR_HI_Write), .in_0(2'b10), .in_1(2'b01), .out(multiplexer_3_out));
  // General_Purpose_Register Instruction_Register__HI: pin names not known; wires that end beside it: demultiplexer_1_out_0, multiplexer_3_out, clk, {IR_HI_3_2, IR_HI_1_0}
  // General_Purpose_Register Instruction_Register__LO: pin names not known; wires that end beside it: demultiplexer_1_out_1, multiplexer_2_out, clk, {IR_LO_3_2, IR_LO_1_0}
  assign not_1_out = ~IR_HI_3_2;  // Not not_1, 2 bits wide
  assign not_2_out = ~IR_HI_3_2;  // Not not_2, 2 bits wide
  not not_3 (not_3_out, IR_LO_1_0[1]);
  xor xor_1 (xor_1_out, IR_LO_1_0[1], IR_LO_1_0[0]);
  Multiplexer #(.Selector_Bits(2), .Bits(8)) multiplexer_4 (
    .sel(IR_HI_1_0), .in_0(8'ha9), .in_1(8'ha6), .in_2(8'h9a), .in_3(8'h6a), .out(multiplexer_4_out));
  and and_1 (and_1_out[2], IR_LO_1_0[0], IR_LO_1_0[1], not_1_out[0], not_1_out[1]);
  and and_2 (and_1_out[1], not_1_out[1], not_1_out[0], IR_LO_1_0[0], not_3_out);
  and and_3 (and_1_out[0], xor_1_out, not_2_out[0], not_2_out[1]);
  and and_4 (and_4_out, IR_HI_3_2[0], IR_HI_3_2[1]);
  Multiplexer #(.Bits(8)) multiplexer_5 (
    .sel(State_Transition_p5), .in_0(8'haa), .in_1(multiplexer_4_out), .out(multiplexer_5_out));
  Multiplexer #(.Bits(2)) multiplexer_6 (.sel(IR_LO_1_0[0]), .in_0(2'b10), .in_1(2'b01), .out(multiplexer_6_out));
  Registe_File Register_File (
    .Clock(clk), .ReadRegister_1(IR_HI_1_0), .ReadRegister_2(IR_LO_3_2), .ControlSignals(multiplexer_5_out),
    .WriteData(multiplexer_8_out), .WriteRegister(IR_HI_1_0), .ReadData_1(Register_File_readdata_1),
    .ReadData_2(Register_File_readdata_2));
  Multiplexer #(.Bits(4)) multiplexer_7 (
    .sel(and_4_out), .in_0(Register_File_readdata_2), .in_1({IR_LO_3_2, IR_LO_1_0}), .out(multiplexer_7_out));
  // ALU_or_something alu_or_something_1: pin names not known; wires that end beside it: multiplexer_7_out, and_1_out, Register_File_readdata_1, ALU_out
  Registers_DRAM Data_Memory (
    .Address_Bus({2'b00, IR_LO_3_2}), .Clock(clk), .Control_Bus(multiplexer_6_out), .Data_Bus(ALU_out),
    .Data_Output(Final_Output));
  Multiplexer #(.Selector_Bits(2), .Bits(4)) multiplexer_8 (
    .sel(IR_HI_3_2), .in_0(ALU_out), .in_1(Final_Output), .in_2({IR_LO_3_2, IR_LO_1_0}), .in_3(Dummy),
    .out(multiplexer_8_out));
endmodule

/* Test case Test:
# --- Test: program Instruction Memory via buses and run a small program ---
# Program:
#   0/1 : LDI R1,#5   (HI=9,  LO=5)
#   2/3 : LDI R2,#3   (HI=10, LO=3)
#   4/5 : ADD R2,R1   (HI=2,  LO=4)  ; ALU_out should be 8 during execute
#   6/7 : SUB R2,R1   (HI=2,  LO=5)  ; ALU_out should be 3 during execute

clk state PC_inc IP InstructionMemory_dataInput InstructionMemory_ctrl IR-HI-Write IR-LO-Write IR_HI[3:2] IR_HI[1:0] IR_LO[3:2] IR_LO[1:0] ALU_out

# =========================================================
# 1. PROGRAM INSTRUCTION MEMORY USING NORMAL INTERFACE
# ---------------------------------------------------------
# We rely on your control unit / PC_inc to step through IF1/IF2,
# and we just provide the data nibble and InstructionMemory_ctrl
# to store HI/LO nibbles at successive addresses.
#
# Addresses and nibbles:
#   addr 0 : 0x9  (HI of LDI R1,#5)
#   addr 1 : 0x5  (LO of LDI R1,#5)
#   addr 2 : 0xA  (HI of LDI R2,#3)
#   addr 3 : 0x3  (LO of LDI R2,#3)
#   addr 4 : 0x2  (HI of ADD R2,R1)
#   addr 5 : 0x4  (LO of ADD R2,R1)
#   addr 6 : 0x2  (HI of SUB R2,R1)
#   addr 7 : 0x5  (LO of SUB R2,R1)
# =========================================================

# Spin FSM / PC into a stable starting state (as you were doing before)
repeat(39) C X X X 0 0 X X X X X X X

# --- FIRST instruction: LDI R1,#5 ---
# addr 0 <- 0x9  (HI of LDI R1,#5)
C X X X 9 1 X X  X X X X X
# addr 1 <- 0x5  (LO of LDI R1,#5)
C X X X 5 1 X X  X X X X X
# next three cycles: decode, execute, writeback – ALU_out don't-care
repeat(3) C X X X 0 0 X X X X X X X

# --- SECOND instruction: LDI R2,#3 ---
# addr 2 <- 0xA  (HI of LDI R2,#3)
C X X X 10 1 X X  X X X X X
# addr 3 <- 0x3  (LO of LDI R2,#3)
C X X X 3  1 X X  X X X X X
# next three cycles: decode, execute, writeback – ALU_out don't-care
repeat(3) C X X X 0 0 X X X X X X X

# --- THIRD instruction: ADD R2,R1 ---
# addr 4 <- 0x2  (HI of ADD R2,R1)
C X X X 2 1 X X  X X X X X
# addr 5 <- 0x4  (LO of ADD R2,R1)
C X X X 4 1 X X  X X X X X
# next three cycles: decode, execute, writeback
# During the EXECUTE cycle of this ADD, ALU_out[3:0] should be 8 (0x8).
# Once you know which 'state' bit = Execute, you can change the Xs
# on the correct cycle to (8) instead of X.
repeat(3) C X X X 0 0 X X X X X X X

# --- FOURTH instruction: SUB R2,R1 ---
# addr 6 <- 0x2  (HI of SUB R2,R1)
C X X X 2 1 X X  X X X X X
# addr 7 <- 0x5  (LO of SUB R2,R1)
C X X X 5 1 X X  X X X X X
# next three cycles: decode, execute, writeback
# During the EXECUTE cycle of this SUB, ALU_out[3:0] should be 3 (0x3).
# Again, once you align this with 'state', you can set ALU_out to 3
# on the right cycle.
repeat(3) C X X X 0 0 X X X X X X X

# =========================================================
# 2. RUN / OBSERVE PHASE (OPTIONAL)
# ---------------------------------------------------------
# At this point, the program is in instruction memory and the CPU
# has already stepped through the IF/ID/EX/WB cycles used during
# programming. If you simply keep clocking, you can watch:
#   - R1 being loaded with 5
#   - R2 being loaded with 3
#   - ADD R2,R1 being executed (ALU_out = 8)
#   - SUB R2,R1 being executed (ALU_out = 3)
#
# Because the exact timing of your FSM may differ, we keep ALU_out
# as don't-care here. Once you know *which* cycle is the execute
# stage for ADD and SUB, you can replace the 'X' in ALU_out with
# 8 and 3 at the appropriate lines.
# ==========================================================

# Example: just keep clocking to let the CPU run
repeat(20) C X X X 0 2 X X X X X X X
*/
