// Digital circuit Registers_DRAM.dig as structural Verilog
module Registers_DRAM (
  input  [3:0] Address_Bus,
  input  Clock,
  input  [1:0] Control_Bus,
  input  [3:0] Data_Bus,
  output [3:0] Data_Output
);

  wire and_1_out, and_2_out, and_3_out, and_4_out, and_5_out, and_6_out, and_7_out, and_8_out, and_9_out,
       and_10_out, and_11_out, and_12_out, and_13_out, and_14_out, and_15_out, and_16_out, decoder_1_out_0,
       decoder_1_out_1, decoder_1_out_2, decoder_1_out_3, decoder_1_out_4, decoder_1_out_5, decoder_1_out_6,
       decoder_1_out_7, decoder_1_out_8, decoder_1_out_9, decoder_1_out_10, decoder_1_out_11,
       decoder_1_out_12, decoder_1_out_13, decoder_1_out_14, decoder_1_out_15;
  wire [3:0] Row_0_p4, Row_1_p4, Row_2_p4, Row_3_p4, Row_4_p4, Row_5_p4, Row_6_p4, Row_7_p4, Row_8_p4,
       Row_9_p4, Row_10_p4, Row_11_p4, Row_12_p4, Row_13_p4, Row_14_p4, Row_15_p4;

  Decoder #(.Selector_Bits(4)) decoder_1 (
    .sel(Address_Bus), .out_0(decoder_1_out_0), .out_1(decoder_1_out_1), .out_2(decoder_1_out_2),
    .out_3(decoder_1_out_3), .out_4(decoder_1_out_4), .out_5(decoder_1_out_5), .out_6(decoder_1_out_6),
    .out_7(decoder_1_out_7), .out_8(decoder_1_out_8), .out_9(decoder_1_out_9), .out_10(decoder_1_out_10),
    .out_11(decoder_1_out_11), .out_12(decoder_1_out_12), .out_13(decoder_1_out_13),
    .out_14(decoder_1_out_14), .out_15(decoder_1_out_15));
  and and_1 (and_1_out, decoder_1_out_0, Clock);
  and and_2 (and_2_out, decoder_1_out_4, Clock);
  and and_3 (and_3_out, decoder_1_out_8, Clock);
  and and_4 (and_4_out, decoder_1_out_12, Clock);
  // General_Purpose_Register Row_0: pin names not known; wires that end beside it: Data_Bus, Control_Bus, and_1_out, Row_0_p4
  // General_Purpose_Register Row_4: pin names not known; wires that end beside it: Data_Bus, Control_Bus, and_2_out, Row_4_p4
  // General_Purpose_Register Row_8: pin names not known; wires that end beside it: Data_Bus, Control_Bus, and_3_out, Row_8_p4
  // General_Purpose_Register Row_12: pin names not known; wires that end beside it: Data_Bus, Control_Bus, and_4_out, Row_12_p4
  and and_5 (and_5_out, decoder_1_out_1, Clock);
  and and_6 (and_6_out, decoder_1_out_5, Clock);
  and and_7 (and_7_out, decoder_1_out_9, Clock);
  and and_8 (and_8_out, decoder_1_out_13, Clock);
  // General_Purpose_Register Row_1: pin names not known; wires that end beside it: Data_Bus, Control_Bus, and_5_out, Row_1_p4
  // General_Purpose_Register Row_5: pin names not known; wires that end beside it: Data_Bus, Control_Bus, and_6_out, Row_5_p4
  // General_Purpose_Register Row_9: pin names not known; wires that end beside it: Data_Bus, Control_Bus, and_7_out, Row_9_p4
  // General_Purpose_Register Row_13: pin names not known; wires that end beside it: Data_Bus, Control_Bus, and_8_out, Row_13_p4
  and and_9 (and_9_out, decoder_1_out_2, Clock);
  and and_10 (and_10_out, decoder_1_out_6, Clock);
  and and_11 (and_11_out, decoder_1_out_10, Clock);
  and and_12 (and_12_out, decoder_1_out_14, Clock);
  // General_Purpose_Register Row_2: pin names not known; wires that end beside it: Data_Bus, Control_Bus, and_9_out, Row_2_p4
  // General_Purpose_Register Row_6: pin names not known; wires that end beside it: Data_Bus, Control_Bus, and_10_out, Row_6_p4
  // General_Purpose_Register Row_10: pin names not known; wires that end beside it: Data_Bus, Control_Bus, and_11_out, Row_10_p4
  // General_Purpose_Register Row_14: pin names not known; wires that end beside it: Data_Bus, Control_Bus, and_12_out, Row_14_p4
  and and_13 (and_13_out, decoder_1_out_3, Clock);
  and and_14 (and_14_out, decoder_1_out_7, Clock);
  and and_15 (and_15_out, decoder_1_out_11, Clock);
  and and_16 (and_16_out, decoder_1_out_15, Clock);
  // General_Purpose_Register Row_3: pin names not known; wires that end beside it: Data_Bus, Control_Bus, and_13_out, Row_3_p4
  // General_Purpose_Register Row_7: pin names not known; wires that end beside it: Data_Bus, Control_Bus, and_14_out, Row_7_p4
  // General_Purpose_Register Row_11: pin names not known; wires that end beside it: Data_Bus, Control_Bus, and_15_out, Row_11_p4
  // General_Purpose_Register Row_15: pin names not known; wires that end beside it: Data_Bus, Control_Bus, and_16_out, Row_15_p4
  Multiplexer #(.Selector_Bits(4), .Bits(4)) multiplexer_1 (
    .sel(Address_Bus), .in_0(Row_0_p4), .in_1(Row_1_p4), .in_2(Row_2_p4), .in_3(Row_3_p4), .in_4(Row_4_p4),
    .in_5(Row_5_p4), .in_6(Row_6_p4), .in_7(Row_7_p4), .in_8(Row_8_p4), .in_9(Row_9_p4), .in_10(Row_10_p4),
    .in_11(Row_11_p4), .in_12(Row_12_p4), .in_13(Row_13_p4), .in_14(Row_14_p4), .in_15(Row_15_p4),
    .out(Data_Output));

  // Notes on the sheet:
  //   DRAM
endmodule
